# Fritzing sketch lights (saved by Fritzing 1.0.1rc)
circuit board: 7cm x 5cm
breadboards: 1

parts:
  BUCK = Adafruit LM3671 Buck Converter [part_number="Adafruit #2745"]
  FET = Basic FET N-Channel [package="TO220 [THT]"]
  FET_2 = Basic FET N-Channel [package="TO220 [THT]"]
  10K = Resistor [tolerance=±5% resistance=10k power=0.25W package=THT]
  10K_2 = Resistor [tolerance=±5% resistance=10k power=0.25W package=THT]
  100 = Resistor [tolerance=±5% resistance=100 power=0.25W package=THT]
  100_2 = Resistor [tolerance=±5% resistance=100 power=0.25W package=THT]
  12V = longpad pin header, 1 pin [form="long pad"]
  J1 = longpad pin header, 4 pins [form="long pad"]
  J2 = longpad pin header, 4 pins [form="long pad"]
  GND = longpad pin header, 1 pin [form="long pad"]
  ESP = mystery part, 30 pins [chip_label=?]

nets:
  12V: BUCK.VIN, 12V.pin1, J1.pin3, J2.pin3
  N1: BUCK.3.3V, ESP.pin1
  GND: BUCK.GND, FET.source, FET_2.source, 10K.Pin_1, 10K_2.Pin_1, J1.pin4, J2.pin4, GND.pin1, ESP.pin2
  N2: FET.gate, 10K_2.Pin_0, 100.Pin_1
  N3: FET.drain, J2.pin2
  N4: FET_2.gate, 10K.Pin_0, 100_2.Pin_1
  N5: FET_2.drain, J1.pin2
  N6: 100.Pin_0, ESP.pin22
  N7: 100_2.Pin_0, ESP.pin23
  N8: J1.pin1, ESP.pin10
  N9: J2.pin1, ESP.pin9

notes:
  G V W D

custom parts:
  Adafruit LM3671 Buck Converter: Your power supply problems just got SUPER SOLVED! This 3.3V Buck Converter Breakout board is great for supplying power to low voltage circuits from a single Li-Ion cell battery or USB power. This chip provides up to 600-mA load current across the entire input voltage range of 3.5 to 5.5V. Great for your portable project, we made this "pin compatible" with the LM1117-3.3V TO-220 chip so you can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
